// Logisim project 1_zadanie_Vanco_Adrian.circ as structural Verilog: 1 circuit, main circuit main
module main (
  input  A,
  input  B,
  input  C,
  input  D,
  output Y,
  output Z,
  output Y_DNF,
  output Z_DNF,
  output Y_KNF,
  output Z_KNF
);

  wire A_B_C_nD_out, A_nC_D_out, B_nC_D_out, n_A_B_out, n_C_nD_out, nA_2_out, nA_D_out, nA_nB_C_out,
       nA_nB_nD_out, nA_nC_out, nA_out, nB_2_out, nB_D_B_nD_out, nB_D_out, nB_nC_out, nB_out, nC_2_out,
       nC_out, nD_2_out, nD_3_out, nD_out;

  not nD (nD_out, D);
  not nC (nC_out, C);
  not nA (nA_out, A);
  not nB (nB_out, B);
  not nD_2 (nD_2_out, D);
  not nB_2 (nB_2_out, B);
  not nC_2 (nC_2_out, C);
  not nA_2 (nA_2_out, A);
  not nD_3 (nD_3_out, D);
  nor n_A_B (n_A_B_out, A, B);
  nor n_C_nD (n_C_nD_out, C, nD_out);
  xor nB_D_B_nD (nB_D_B_nD_out, B, D);
  and A_nC_D (A_nC_D_out, A, nC_out, D);
  and B_nC_D (B_nC_D_out, B, nC_out, D);
  and nA_nB_C (nA_nB_C_out, nA_out, nB_out, C);
  and nA_nB_nD (nA_nB_nD_out, nA_out, nB_out, nD_2_out);
  or A_B_C_nD (A_B_C_nD_out, A, B, C, nD_3_out);
  or nB_D (nB_D_out, nB_2_out, D);
  or nB_nC (nB_nC_out, nB_2_out, nC_2_out);
  or nA_D (nA_D_out, nA_2_out, D);
  or nA_nC (nA_nC_out, nA_2_out, nC_2_out);
  xor nn_A_B__n_C_nD__n_A_B__nn_C_nD (Y, n_A_B_out, n_C_nD_out);
  nand n_n_C_nD___nB_D_B_nD (Z, n_C_nD_out, nB_D_B_nD_out);
  or A_nC_D_B_nC_D_nA_nB_C_nA_nB_nD (Y_DNF, A_nC_D_out, B_nC_D_out, nA_nB_C_out, nA_nB_nD_out);
  or B_C_nD (Z_DNF, B, C, nD_2_out);
  or B_C_nD_2 (Z_KNF, B, C, nD_3_out);
  and A_B_C_nD___nB_D___nB_nC___nA_D___nA_nC (Y_KNF, A_B_C_nD_out, nB_D_out, nB_nC_out, nA_D_out, nA_nC_out);

  // Notes on the sheet:
  //   ZADANIE
  //   DNF
  //   KNF
endmodule
