// Logisim project 2_zadanie_Vanco_Adrian.circ as structural Verilog: 1 circuit, main circuit main
module main (
  input  a,
  input  b,
  input  c,
  input  d,
  output A_D,
  output B_D,
  output C_D,
  output D_D,
  output A_K,
  output B_K,
  output C_K,
  output D_K
);

  wire n_a_b_c_out, n_a_b_out, n_a_c_out, n_b_c_out, n_b_nc_out, n_nb_c_out, n_nb_nc_out, na_out, nb_2_out,
       nb_out, nc_2_out, nc_out;

  nand na (na_out, a, a);
  nand nb (nb_out, b, b);
  nor nb_2 (nb_2_out, b, b);
  nand nc (nc_out, c, c);
  nor nc_2 (nc_2_out, c, c);
  nand n_b_c (n_b_c_out, b, c);
  nand n_b_nc (n_b_nc_out, b, nc_out);
  nand n_nb_c (n_nb_c_out, nb_out, c);
  nor n_a_b (n_a_b_out, a, b);
  nor n_a_c (n_a_c_out, a, c);
  nor n_a_b_c (n_a_b_c_out, a, b, c);
  nor n_nb_nc (n_nb_nc_out, nb_2_out, nc_2_out);
  nand n_na_n_b_c__n_b_nc (A_D, na_out, n_b_c_out, n_b_nc_out);
  nand n_na_n_b_c (B_D, na_out, n_b_c_out);
  nand n_na_n_b_nc__n_nb_c (C_D, na_out, n_nb_c_out, n_b_nc_out);
  nor n_n_a_b__n_a_b (A_K, n_a_b_out, n_a_b_out);
  nor n_n_a_b__n_a_c (B_K, n_a_b_out, n_a_c_out);
  nor n_n_a_b_c__n_nb_nc (C_K, n_a_b_c_out, n_nb_nc_out);

  assign D_D = d;
  assign D_K = d;

  // Notes on the sheet:
  //   DNF
  //   KNF
endmodule
