// Logisim project 3_zadanie_Vanco_Adrian.circ as structural Verilog: 1 circuit, main circuit main
module main (
  input  X,
  input  Res,
  output Y
);

  wire CLK_out, j_k_ff_1_q, j_k_ff_1_qn, j_k_ff_2_q, j_k_ff_2_qn, j_k_ff_3_q, nand_1_out, nand_2_out,
       nand_3_out, nand_4_out, nand_5_out, nand_6_out, nand_7_out, nand_8_out, nand_10_out, nand_11_out,
       nand_12_out, nand_13_out, nand_14_out, nand_15_out;

  nand nand_1 (nand_1_out, X, X);
  Clock CLK (.out(CLK_out));
  nand nand_2 (nand_2_out, j_k_ff_1_q, j_k_ff_2_q);
  nand nand_3 (nand_3_out, j_k_ff_2_q, j_k_ff_3_q, X);
  nand nand_4 (nand_4_out, j_k_ff_2_q, nand_1_out);
  nand nand_5 (nand_5_out, j_k_ff_3_q, nand_1_out);
  nand nand_6 (nand_6_out, j_k_ff_1_q, j_k_ff_2_qn);
  nand nand_7 (nand_7_out, j_k_ff_2_qn, X);
  nand nand_8 (nand_8_out, j_k_ff_1_qn, j_k_ff_2_q);
  nand nand_9 (Y, nand_2_out, nand_2_out);
  nand nand_10 (nand_10_out, nand_3_out, nand_3_out);
  nand nand_11 (nand_11_out, nand_4_out, nand_7_out);
  nand nand_12 (nand_12_out, nand_5_out, nand_5_out);
  nand nand_13 (nand_13_out, nand_5_out, nand_2_out, nand_1_out);
  nand nand_14 (nand_14_out, nand_6_out, nand_7_out, nand_8_out);
  nand nand_15 (nand_15_out, nand_8_out, nand_5_out);
  J_K_Flip_Flop j_k_ff_1 (
    .J(nand_10_out), .clk(CLK_out), .K(nand_11_out), .Q(j_k_ff_1_q), .Qn(j_k_ff_1_qn), .reset(Res));  // open: preset, en
  J_K_Flip_Flop j_k_ff_2 (
    .J(nand_12_out), .clk(CLK_out), .K(nand_13_out), .Q(j_k_ff_2_q), .Qn(j_k_ff_2_qn), .reset(Res));  // open: preset, en
  J_K_Flip_Flop j_k_ff_3 (
    .J(nand_14_out), .clk(CLK_out), .K(nand_15_out), .Q(j_k_ff_3_q), .reset(Res));  // open: Qn, preset, en
endmodule
